# Fritzing sketch Wassertonne (saved by Fritzing 0.9.4)

parts:
  Bauteil1 = Arduino Uno (Rev3)
  M1 = DC Motor
  R1 = Resistor [tolerance=±5% resistance=1k package=THT]
  R2 = Resistor [tolerance=±5% resistance=1k package=THT]
  LED1 = LED - 5mm [color="Yellow (592nm)" package="5 mm [THT]"]
  LED2 = LED - 5mm [color="Red (633nm)" package="5 mm [THT]"]
  LED3 = LED - 5mm [color="Green (560nm)" package="5 mm [THT]"]
  Part1 = KY-019 5V Relay Module [package="Breakout board"]
  Power_plug1 = Power plug
  R3 = Resistor [tolerance=±5% resistance=220 package=THT]
  R4 = Resistor [tolerance=±5% resistance=220 package=THT]
  R5 = Resistor [tolerance=±5% resistance=220 package=THT]
  S1 = Tilt Switch [package=THT]
  S2 = Tilt Switch [package=THT]

nets:
  N1: Bauteil1.D8, R1.Pin_1, S2.Pin_1
  N2: Bauteil1.D9_PWM, R2.Pin_1, S1.Pin_1
  N3: Bauteil1.D11_PWM/MOSI, R1.Pin_0, R2.Pin_0
  N4: Bauteil1.D13/SCK, R4.Pin_1
  GND: Bauteil1.GND, LED1.cathode, LED2.cathode, LED3.cathode, Part1.-, Part1.Common, Power_plug1.GND, S1.Pin_2, S2.Pin_2
  N5: Bauteil1.D5_PWM, Part1.S
  N6: Bauteil1.D6_PWM, R3.Pin_1
  N7: Bauteil1.D7, R5.Pin_1
  N8: Bauteil1.5V, Part1.+
  VIN: Bauteil1.VIN, M1.pin_1, Power_plug1.VCC
  N9: M1.pin_2, Part1.NC
  N10: LED1.anode, R4.Pin_0
  N11: LED2.anode, R5.Pin_0
  N12: LED3.anode, R3.Pin_0

notes:
  LED
  Status
  Voll
  Pumpe
  Schwimmschalter Vorfilter
  Schwimmschalter Tonne

custom parts:
  KY-019 5V Relay Module: KY-019 5V Relay module, used to control AC circuits.
